# Fritzing sketch Radar_Sensor_Schematic (saved by Fritzing 1.0.6)

parts:
  Mod1 = Raspberry Pi 4B
  A1 = Ai-thinker Rd-03D

nets:
  N1: Mod1.5V, A1.Pin_7, A1.Pin_8
  N2: Mod1.GND, A1.Pin_3, A1.Pin_9
  N3: Mod1.GPIO14, A1.Pin_2, A1.Pin_10
  N4: Mod1.GPIO15, A1.Pin_1, A1.Pin_11

notes:
  GND
  5V
  RX
  TX
  TX
  RX

custom parts:
  Ai-thinker Rd-03D: Rd-03D is a radar module developed by Shenzhen Ai-Thinker Technology Co., LTD, which is equipped with the S5KM312CL chip. S5KM312CL is an integrated microcontroller millimeter wave sensor SoC based on FMCW radar transceiver technology.
